# Fritzing sketch Sketch hardware (saved by Fritzing 0.9.5d)

parts:
  Part2 = ACS712 Current Sensor 5A 20A 30A
  U1 = NodeMCU V3.0

nets:
  N1: Part2.2, Part2.OUT, U1.A0
  VCC: Part2.VCC, U1.3V3
  GND: Part2.GND, U1.GND

custom parts:
  ACS712 Current Sensor 5A 20A 30A: Remix by Michael Kubina http://www.kubina.info Original by: https://forum.fritzing.org/t/current-sensor-5a-acs712/7694 https://forum.fritzing.org/u/ArtHome ArtHome12@gmail.com
  NodeMCU V3.0: ESP8266 based NodeMCU
